# Fritzing sketch 33-HandScanner (saved by Fritzing 1.0.6)
breadboards: 1

parts:
  Ledstrip = SMD RGB LED (WS2812) [package=5050]
  knop = Square Pushbutton
  R9 = Resistor [tolerance=±5% resistance=470 package="0603 [SMD]"]
  1000uF_25V = Capacitor Polarized [package=panasonic_g]
  R13 = Resistor [tolerance=±5% resistance=470k package="0603 [SMD]"]  # not connected
  Nano = Arduino Micro (Rev3)

nets:
  N1: Ledstrip.DIn, R9.Pin_1
  12V: Ledstrip.VCC
  GND: Ledstrip.VSS, knop.leg1, 1000uF_25V.-
  N2: R9.Pin_0, Nano.A0

notes:
  Spiegel
  TouchPlaat
