# Fritzing sketch 47a-KikkerkokenInput (saved by Fritzing 1.0.6)
breadboards: 1

parts:
  Lestrip_warmwit = SMD RGB LED (WS2812) [package=5050]
  Ledstrip_RGB = SMD RGB LED (WS2812) [package=5050]
  4a = Square Pushbutton  # not connected
  3b = Square Pushbutton  # not connected
  3a = Square Pushbutton  # not connected
  2b = Square Pushbutton  # not connected
  2a = Square Pushbutton  # not connected
  1b = Square Pushbutton  # not connected
  1a = Square Pushbutton  # not connected
  Start = Square Pushbutton
  R4 = Resistor [tolerance=±5% resistance=470 package="0603 [SMD]"]
  R5 = Resistor [tolerance=±5% resistance=470 package="0603 [SMD]"]
  1000uF_25V = Capacitor Polarized [package=panasonic_g]
  1000uF_25V_2 = Capacitor Polarized [package=panasonic_g]
  4b = Square Pushbutton  # not connected
  Nano = Arduino Pro Mini v13

nets:
  N1: Lestrip_warmwit.DIn, R4.Pin_1
  5V: Lestrip_warmwit.VCC, Ledstrip_RGB.VCC, 1000uF_25V.+, 1000uF_25V_2.+
  N2: Lestrip_warmwit.VSS, Start.leg1, 1000uF_25V_2.-
  N3: Ledstrip_RGB.DIn, R5.Pin_1
  N4: Ledstrip_RGB.VSS, 1000uF_25V.-
  N5: R4.Pin_0, Nano.D11_PWM/MOSI
  N6: R5.Pin_0, Nano.D12/MISO
