# Fritzing sketch 47b-KikkerkokenOutput (saved by Fritzing 1.0.6)
breadboards: 1

parts:
  Strip_1 = SMD RGB LED (WS2812) [package=5050]
  Ledstrip_2 = SMD RGB LED (WS2812) [package=5050]
  4a = Square Pushbutton
  3a = Square Pushbutton
  2a = Square Pushbutton
  1a = Square Pushbutton
  0a = Square Pushbutton
  R4 = Resistor [tolerance=±5% resistance=470 package="0603 [SMD]"]
  R5 = Resistor [tolerance=±5% resistance=470 package="0603 [SMD]"]
  1000uF_25V = Capacitor Polarized [package=panasonic_g]
  1000uF_25V_2 = Capacitor Polarized [package=panasonic_g]
  Nano = Arduino Uno (Rev3)

nets:
  N1: Strip_1.DIn, R4.Pin_1
  VCC: Strip_1.VCC, Ledstrip_2.VCC, 1000uF_25V.+, 1000uF_25V_2.+
  N2: Strip_1.VSS, 4a.leg1, 3a.leg1, 2a.leg1, 1a.leg1, 0a.leg1, 1000uF_25V_2.-
  N3: Ledstrip_2.DIn, R5.Pin_1
  N4: Ledstrip_2.VSS, 1000uF_25V.-
  N5: 4a.leg0, Nano.D6_PWM
  N6: 3a.leg0, Nano.D5_PWM
  N7: 2a.leg0, Nano.D4
  N8: 1a.leg0, Nano.D3_PWM
  N9: 0a.leg0, Nano.D2
  N10: R4.Pin_0, Nano.D11_PWM/MOSI
  N11: R5.Pin_0, Nano.D12/MISO
  5V: Nano.5V
